// Logisim project adder.circ as structural Verilog: 3 circuits, main circuit four_bit_adder
module half_adder (
  input  A,
  input  B,
  output S,
  output Cout
);

  and and_1 (Cout, B, A);
  xor xor_1 (S, A, B);
endmodule

module full_adder (
  input  A,
  input  B,
  input  Cin,
  output S,
  output Cout
);

  wire and_1_out, and_2_out, xor_1_out;

  xor xor_1 (xor_1_out, A, B);
  and and_1 (and_1_out, A, B);
  xor xor_2 (S, xor_1_out, Cin);
  and and_2 (and_2_out, xor_1_out, Cin);
  or or_1 (Cout, and_2_out, and_1_out);
endmodule

module four_bit_adder (
  input  in_1,
  input  in_2,
  input  in_3,
  input  in_4,
  input  in_5,
  input  in_6,
  input  in_7,
  input  in_8
);

  wire full_adder_2_cout, full_adder_3_cout, half_adder_1_cout;
  wire [3:0] half_adder_1_s;

  full_adder full_adder_1 (.A(in_1), .B(in_5), .Cin(full_adder_2_cout), .S(half_adder_1_s[3]));  // open: Cout
  full_adder full_adder_2 (
    .A(in_2), .B(in_6), .Cin(full_adder_3_cout), .S(half_adder_1_s[2]), .Cout(full_adder_2_cout));
  full_adder full_adder_3 (
    .A(in_3), .B(in_7), .Cin(half_adder_1_cout), .S(half_adder_1_s[1]), .Cout(full_adder_3_cout));
  Hex_Digit_Display hex_digit_display_1 (.value(half_adder_1_s));  // open: dp
  half_adder half_adder_1 (.A(in_4), .B(in_8), .Cout(half_adder_1_cout), .S(half_adder_1_s[0]));
endmodule
